# Fritzing sketch DHT11 (saved by Fritzing 0.8.7b)
breadboards: 1

parts:
  부품1 = Arduino Uno (Rev3)
  DHT1 = DHT11 Humitidy and Temperature Sensor

nets:
  N1: 부품1.D6_PWM, DHT1.DATA
  5V: 부품1.5V, DHT1.VDD
  GND: 부품1.GND, DHT1.GND

custom parts:
  DHT11 Humitidy and Temperature Sensor: DHT11 Humidity and Temperature Sensor
