# Fritzing sketch DHT11_lcd (saved by Fritzing 0.8.7b)
breadboards: 1

parts:
  부품1 = Arduino Uno (Rev3)
  DHT1 = DHT11 Humitidy and Temperature Sensor
  부품3 = LCD1602-I2C

nets:
  N1: 부품1.A4/SDA, 부품3.SDA
  N2: 부품1.A5/SCL, 부품3.SCL
  N3: 부품1.D6_PWM, DHT1.DATA
  5V: 부품1.5V, DHT1.VDD, 부품3.VCC
  GND: 부품1.GND, DHT1.GND, 부품3.GND

custom parts:
  DHT11 Humitidy and Temperature Sensor: DHT11 Humidity and Temperature Sensor
  LCD1602-I2C: A standard character display, usually with 2x16 characters. Comes in many colors with LCM1602 IIC attached.
